// Logisim project Lab7.circ as structural Verilog: 2 circuits, main circuit ParityGenerator
module XOR (
  input  X,
  input  Y,
  output out_3
);

  wire and_1_out, and_2_out, not_1_out, not_2_out;

  not not_1 (not_1_out, Y);
  not not_2 (not_2_out, X);
  and and_1 (and_1_out, not_2_out, Y);
  and and_2 (and_2_out, X, not_1_out);
  or or_1 (out_3, and_1_out, and_2_out);

  // Notes on the sheet:
  //   Use minterm expansion to create an XOR gate using AND + OR gates
endmodule

module ParityGenerator (
  input  X,
  input  Y,
  input  Z,
  output Parity
);

  wire xor_1_out_3;

  XOR xor_1 (.out_3(xor_1_out_3), .X(X), .Y(Y));
  XOR xor_2 (.out_3(Parity), .X(xor_1_out_3), .Y(Z));

  // Notes on the sheet:
  //   Input Bits
  //   -Adam Woo
  //   Output Bit
  //   I pledge my honor that I have abided by the Stevens Honor System
  //   Write your parity circuit here
  //   the output = 1 if an odd number of inputs (1 or 3) are 1, otherwise 0
  //   ONLY use: NOT, AND, OR, and any custom functions you write (included in the .circ submission)
  //   SMILE
  //   WRITE YOUR NAME AND PLEDGE SOMEWHERE IN THIS CIRCUIT
endmodule
